// Logisim project single_cycle.circ as structural Verilog: 3 circuits, main circuit main
module main (
);

  wire and_1_out, clock_1_out, control_1_alusrc, control_1_branch, control_1_memread, control_1_memtoreg,
       control_1_memwrite, mips_alu_1_p4, registerfile_1_p3;
  wire [1:0] control_1_aluop;
  wire [3:0] mips_alu_1_p3;
  wire [31:0] adder_1_out, adder_2_out, mips_alu_1_p5, mips_ram_1_p4, mipsprogramrom_1_p2, multiplexer_1_out,
       multiplexer_2_out, PC_q, registerfile_1_p1, registerfile_1_p4;

  Counter #(.width(32), .max('hffffffff)) PC (
    .load(1'b1), .D(multiplexer_2_out), .count(1'b0), .Q(PC_q), .clk(clock_1_out), .clr(1'b0));  // open: carry
  Clock clock_1 (.out(clock_1_out));
  Adder #(.width(32)) adder_1 (.a(PC_q), .b(32'h4), .out(adder_1_out));  // open: cin, cout
  // MIPSProgramROM mipsprogramrom_1: pin names not known; wires that end beside it: PC_q, mipsprogramrom_1_p2
  Control control_1 (
    .Instruction(mipsprogramrom_1_p2), .Branch(control_1_branch), .MemRead(control_1_memread),
    .MemtoReg(control_1_memtoreg), .ALUOp(control_1_aluop), .MemWrite(control_1_memwrite),
    .ALUSrc(control_1_alusrc));  // open: RegDst, RegWrite
  // RegisterFile registerfile_1: pin names not known; wires that end beside it: registerfile_1_p1, clock_1_out, registerfile_1_p3, registerfile_1_p4
  Multiplexer #(.width(32)) multiplexer_1 (
    .in0(registerfile_1_p4), .out(multiplexer_1_out), .sel(control_1_alusrc));  // open: in1
  Adder #(.width(32)) adder_2 (.a(adder_1_out), .out(adder_2_out));  // open: b, cin, cout
  // Mips_ALU mips_alu_1: pin names not known; wires that end beside it: registerfile_1_p3, multiplexer_1_out, mips_alu_1_p3, mips_alu_1_p4, mips_alu_1_p5, mips_alu_1_p5
  ALU_control alu_control_1 (.Instruction(mipsprogramrom_1_p2), .ALUop(control_1_aluop), .Output(mips_alu_1_p3));
  Multiplexer #(.width(32)) multiplexer_2 (
    .in0(adder_1_out), .in1(adder_2_out), .out(multiplexer_2_out), .sel(and_1_out));
  and and_1 (and_1_out, control_1_branch, mips_alu_1_p4);
  // MIPS_RAM #(.addrWidth(24)) mips_ram_1: pin names not known; wires that end beside it: control_1_memwrite, control_1_memread, clock_1_out, mips_ram_1_p4
  Multiplexer #(.width(32)) multiplexer_3 (
    .in0(mips_ram_1_p4), .in1(mips_alu_1_p5), .out(registerfile_1_p1), .sel(control_1_memtoreg));

  // Notes on the sheet:
  //   Jeg kan ikke gennemskue dens input...
  //   contents of mipsprogramrom_1 (hex, n*v repeats v):
  //   lw $1,0($2)
  //   Hmm...?
endmodule

module Control (
  input  [31:0] Instruction,
  output RegDst,
  output Branch,
  output MemRead,
  output MemtoReg,
  output [1:0] ALUOp,
  output MemWrite,
  output ALUSrc,
  output RegWrite
);

  // PLA #(.in_width(32), .out_width(1), .truth_table("000000xxxxxxxxxxxxxxxxxxxxxxxxxx,1#R-type")) pla_1: pin names not known; wires that end beside it: RegDst
  // PLA #(.in_width(32), .out_width(1), .truth_table("000100xxxxxxxxxxxxxxxxxxxxxxxxxx,1#beq")) pla_2: pin names not known; wires that end beside it: Branch
  // PLA #(.in_width(32), .out_width(1), .truth_table("100011xxxxxxxxxxxxxxxxxxxxxxxxxx,1#lw")) pla_3: pin names not known; wires that end beside it: MemRead
  // PLA #(.in_width(32), .out_width(1), .truth_table("100011xxxxxxxxxxxxxxxxxxxxxxxxxx,1#lw")) pla_4: pin names not known; wires that end beside it: MemtoReg
  // PLA #(.in_width(32), .truth_table("000000xxxxxxxxxxxxxxxxxxxxxxxxxx,10#R-type\n000100xxxxxxxxxxxxxxxxxxxxxxxxxx,01#beq")) pla_5: pin names not known; wires that end beside it: ALUOp
  // PLA #(.in_width(32), .out_width(1), .truth_table("101011xxxxxxxxxxxxxxxxxxxxxxxxxx,1#sw")) pla_6: pin names not known; wires that end beside it: MemWrite
  // PLA #(.in_width(32), .out_width(1), .truth_table("100011xxxxxxxxxxxxxxxxxxxxxxxxxx,1#lw\n101011xxxxxxxxxxxxxxxxxxxxxxxxxx,1#sw")) pla_7: pin names not known; wires that end beside it: ALUSrc
  // PLA #(.in_width(32), .out_width(1), .truth_table("000000xxxxxxxxxxxxxxxxxxxxxxxxxx,1#R-type\n100011xxxxxxxxxxxxxxxxxxxxxxxxxx,0#lw")) pla_8: pin names not known; wires that end beside it: RegWrite

  // Notes on the sheet:
  //   TODO: Implementer resterende instruktioner.
endmodule

module ALU_control (
  input  [31:0] Instruction,
  input  [1:0] ALUop,
  output [3:0] Output
);


  // Notes on the sheet:
  //   TODO: Implementer ALU control.
endmodule
